# Fritzing sketch modelo-fritzing (saved by Fritzing 0.9.3b)
breadboards: 1

parts:
  Componente1 = Arduino Uno (Rev3)
  R1 = Photocell (LDR) [package=THT]
  R2 = Photocell (LDR) [package=THT]
  4_Channel_Relay1 = 4 Channel Power Relay
  LD1 = LD
  LD2 = LD
  S1 = Reed switch [package=THT]
  S2 = SWITCH-MOMENTARY-2 [package=reed_switch_pth]
  R3 = Resistor [tolerance=±5% resistance=330 package="2512 [SMD]"]
  R4 = Resistor [tolerance=±5% resistance=330 package="2512 [SMD]"]
  R5 = Resistor [tolerance=±5% resistance=330 package="2512 [SMD]"]
  R6 = Resistor [tolerance=±5% resistance=330 package="2512 [SMD]"]
  R7 = Resistor [tolerance=±5% resistance=1k package="2512 [SMD]"]
  R8 = Resistor [tolerance=±5% resistance=1k package="2512 [SMD]"]
  R9 = Resistor [tolerance=±5% resistance=1k package="2512 [SMD]"]
  R10 = Resistor [tolerance=±5% resistance=1k package="2512 [SMD]"]

nets:
  N1: Componente1.A0, R1.pin_1, R7.Pin_0
  N2: Componente1.A1, R2.pin_1, R8.Pin_0
  N3: Componente1.D12/MISO, R3.Pin_1
  N4: Componente1.D13/SCK, R4.Pin_1
  N5: Componente1.D6_PWM, S2.2, R10.Pin_0
  N6: Componente1.D7, S1.pin_2, R9.Pin_0
  5V: Componente1.5V, 4_Channel_Relay1.VCC, R5.Pin_1, R6.Pin_1, R7.Pin_1, R8.Pin_1
  GND: Componente1.GND, R1.pin_0, R2.pin_0, 4_Channel_Relay1.GND, LD1.cathode, LD2.cathode, R9.Pin_1, R10.Pin_1
  N7: 4_Channel_Relay1.IN1, R4.Pin_0
  N8: 4_Channel_Relay1.IN2, R3.Pin_0
  N9: LD1.anode, R5.Pin_0
  N10: LD2.anode, R6.Pin_0

custom parts:
  4 Channel Power Relay: A 4 channel power relay. The module operates at 5V.
  LD: A Generic Red Dot Laser Diode Module (~5mW)
